// Logisim project simple_processor.circ as structural Verilog: 7 circuits, main circuit simple CPU
module simple_CPU (
);

  wire clk, rst;
  wire [3:0] ALU_OP, alu_out, read_reg_addr, reg_val, val, write_reg_addr;
  wire [7:0] program_counter_q;
  wire [15:0] rom_1_data;

  Button u_clk (.out(clk));
  Button reset (.out(rst));
  // Probe on program_counter_q
  program_counter program_counter (.count(clk), .clk(clk), .reset(rst), .Q(program_counter_q));  // open: load, D
  bus instruction_bus ();  // open: D_en, in, D, out
  cache cache (.clk(clk), .reset(rst));  // open: in, ld, addr, out
  bus mem_bus ();  // open: D_en, in, D, out
  ROM #(.dataWidth(16)) rom_1 (.addr(program_counter_q), .data(rom_1_data));  // open: sel
  Button start ();  // open: out
  // Probe on rom_1_data
  ctrl ctrl (.instruction(rom_1_data), .val(val), .Addr0(write_reg_addr), .Addr1(read_reg_addr), .opcode(ALU_OP));
  ALU ALU (.OP(ALU_OP), .D0(reg_val), .D1(val), .Q(alu_out));
  // Probe on alu_out
  // Probe on reg_val
  registers reg_0_7 (
    .clk(clk), .reset(rst), .D(alu_out), .sel_write(write_reg_addr), .sel_read(read_reg_addr), .D_2(reg_val));

  // Notes on the sheet:
  //   TODO
  //   contents of rom_1 (hex, n*v repeats v):
  //   3004 4012
endmodule

module program_counter (
  input  load,
  input  [7:0] D,
  input  count,
  input  clk,
  input  reset,
  output [7:0] Q
);

  Counter counter_1 (.load(load), .D(D), .count(count), .Q(Q), .clk(clk), .clr(reset));  // open: carry

  // Notes on the sheet:
  //   Use load as an address pointer?
endmodule

module bus (
  input  D_en,
  input  [7:0] D,
  input  [7:0] in,
  output [7:0] out
);

  // Transmission_Gate #(.width(8)) transmission_1: pin names not known; wires that end beside it: D_en, D, in, D_en

  assign out = in;

  // Other names for the same wires on the sheet: Data_Ctrl = D_en

  // Notes on the sheet:
  //   TODO: Replace with buffer
endmodule

module ALU (
  input  [3:0] OP,
  input  [3:0] D0,
  input  [3:0] D1,
  output [3:0] Q
);

  wire [3:0] adder_1_out, divider_1_out, multiplier_1_out, subtractor_1_out;

  Adder #(.width(4)) adder_1 (.a(D0), .b(D1), .out(adder_1_out));  // open: cin, cout
  Subtractor #(.width(4)) subtractor_1 (.a(D0), .b(D1), .out(subtractor_1_out));  // open: bin, bout
  Multiplier #(.width(4)) multiplier_1 (.a(D0), .b(D1), .out(multiplier_1_out));  // open: cin, cout
  Divider #(.width(4)) divider_1 (.a(D0), .b(D1), .out(divider_1_out));  // open: upper, rem
  BitAdder bitadder_1 ();  // open: in0, out
  Negator negator_1 ();  // open: in, out
  Comparator comparator_1 ();  // open: a, b, gt, eq, lt
  Shifter shifter_1 ();  // open: in, dist, out
  Multiplexer #(.select(4), .width(4), .enable("false")) multiplexer_1 (
    .in1(4'b0000), .in2(4'b0001), .in3(adder_1_out), .in4(subtractor_1_out), .in5(multiplier_1_out),
    .in6(divider_1_out), .out(Q), .sel(OP));  // open: in0, in7, in8, in9, in10, in11, in12, in13, in14, in15
endmodule

module registers (
  input  clk,
  input  reset,
  input  [3:0] D,
  input  [3:0] sel_write,
  input  [3:0] sel_read,
  output [3:0] D_2
);

  wire Reg_0, Reg_1, Reg_2, Reg_3, Reg_4, Reg_5, Reg_6, Reg_7;
  wire [3:0] reg_0_t, reg_1_t, reg_2_t, reg_3_t, reg_4_t, reg_5_t, reg_6_t, reg_7_t;

  Decoder #(.select(4), .enable("false")) decoder_1 (
    .out0(Reg_0), .out1(Reg_1), .out2(Reg_2), .out3(Reg_3), .out4(Reg_4), .out5(Reg_5), .out6(Reg_6),
    .out7(Reg_7), .sel(sel_write));  // open: out8, out9, out10, out11, out12, out13, out14, out15
  Register #(.width(4)) u_Reg_0 (.D(D), .en(Reg_0), .Q(reg_0_t), .clk(clk), .clr(reset));
  Register #(.width(4)) u_Reg_2 (.D(D), .en(Reg_2), .Q(reg_2_t), .clk(clk), .clr(reset));
  Register #(.width(4)) u_Reg_4 (.D(D), .en(Reg_4), .Q(reg_4_t), .clk(clk), .clr(reset));
  Register #(.width(4)) u_Reg_6 (.D(D), .en(Reg_6), .Q(reg_6_t), .clk(clk), .clr(reset));
  Register #(.width(4)) u_Reg_1 (.D(D), .en(Reg_1), .Q(reg_1_t), .clk(clk), .clr(reset));
  Register #(.width(4)) u_Reg_3 (.D(D), .en(Reg_3), .Q(reg_3_t), .clk(clk), .clr(reset));
  Register #(.width(4)) u_Reg_5 (.D(D), .en(Reg_5), .Q(reg_5_t), .clk(clk), .clr(reset));
  Register #(.width(4)) u_Reg_7 (.D(D), .en(Reg_7), .Q(reg_7_t), .clk(clk), .clr(reset));
  Multiplexer #(.select(4), .width(4), .enable("false")) multiplexer_1 (
    .in0(reg_0_t), .in1(reg_1_t), .in2(reg_2_t), .in3(reg_3_t), .in4(reg_4_t), .in5(reg_5_t), .in6(reg_6_t),
    .in7(reg_7_t), .out(D_2), .sel(sel_read));  // open: in8, in9, in10, in11, in12, in13, in14, in15

  // Other names for the same wires on the sheet: Data[3:0] = D; rst = reset
endmodule

module cache (
  input  [7:0] in,
  input  ld,
  input  [7:0] addr,
  input  clk,
  input  reset,
  output [7:0] out
);

  wire not_1_out;

  assign out = ld ? in : 8'bz;  // Controlled_Buffer controlled_buffer_1
  not not_1 (not_1_out, ld);
  RAM ram_1 (.addr(addr), .data(out), .clk(clk), .ld(not_1_out), .clr(reset));  // open: sel

  // Notes on the sheet:
  //   Reference: Logisim library documentation
endmodule

module ctrl (
  input  [15:0] instruction,
  output [3:0] val,
  output [3:0] Addr0,
  output [3:0] Addr1,
  output [3:0] opcode
);


  assign Addr0 = instruction[7:4];
  assign Addr1 = instruction[11:8];
  assign opcode = instruction[15:12];
  assign val = instruction[3:0];
endmodule
